# Fritzing sketch Motion_Alarm_fritzing_circuit (saved by Fritzing 0.9.4)
breadboards: 1

parts:
  Part1 = Arduino Uno (Rev3) - ICSP
  SIM800L1 = SIM800L
  R1 = Resistor [tolerance=±5% resistance=220 package=THT]
  M1 = RioRand LM2596
  Power_plug1 = Power plug
  R2 = Resistor [tolerance=±5% resistance=220 package=THT]  # not connected
  PIR1 = PIR sensor
  J1 = Piezo Speaker
  LED1 = LEDs [package=led10mm]
  R3 = Resistor [tolerance=±5% resistance=220 package="0402 [SMD]"]
  C1 = Capacitor Polarized [package=cpol-radial-1000uf-25v]

nets:
  N1: Part1.ICSP_MISO, Part1.D12/MISO, J1.pin2
  N2: Part1.D8, PIR1.SIG
  N3: Part1.D11_PWM/MOSI, R3.Pin_0
  N4: Part1.GND, LED1.C
  N5: Part1.D2, R1.Pin_0
  N6: Part1.D3_PWM, SIM800L1.TXD
  N7: Part1.D7, SIM800L1.RST
  5V: Part1.5V, PIR1.VDD
  N8: SIM800L1.VCC, M1.Pin_3
  N9: SIM800L1.RXD, R1.Pin_1
  N10: SIM800L1.GND, M1.Pin_4
  N11: M1.Pin_1, Power_plug1.VCC
  N12: M1.Pin_2, Power_plug1.GND
  N13: PIR1.GND, J1.pin1, C1.+, C1.-

custom parts:
  SIM800L: SIM800L is a miniature cellular module which allows for GPRS transmission, sending and receiving SMS and making and receiving voice calls. Low cost and small footprint and quad band frequency support make this module perfect solution for any project that require long range connectivity. After connecting power module boots up, searches for cellular network and login automatically. On board LED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

// code stored in the sketch: Untitled3.ino
#include <SoftwareSerial.h>

//Create software serial object to communicate with SIM800L
SoftwareSerial mySerial(3, 2);  //SIM800L Tx & Rx is connected to Arduino #3 & #2

void setup() {
  //Begin serial communication with Arduino and Arduino IDE (Serial Monitor)
  Serial.begin(9600);

  //Begin serial communication with Arduino and SIM800L
  mySerial.begin(9600);

  Serial.println("Initializing...");
  delay(1000);

  mySerial.println("AT");  //Once the handshake test is successful, it will back to OK
  updateSerial();

  mySerial.println("AT+CMGF=1");  // Configuring TEXT mode
  updateSerial();
  mySerial.println("AT+CMGS=\"+ZZxxxxxxxxxx\"");  //change ZZ with country code and xxxxxxxxxxx with phone number to sms
  updateSerial();
  mySerial.print("Last Minute Engineers | lastminuteengineers.com");  //text content
  updateSerial();
  mySerial.write(26);
}

void loop() {
}

void updateSerial() {
  delay(500);
  while (Serial.available()) {
    mySerial.write(Serial.read());  //Forward what Serial received to Software Serial Port
  }
  while (mySerial.available()) {
    Serial.write(mySerial.read());  //Forward what Software Serial received to Serial Port
  }
}
